# Fritzing sketch Esquema_Monitoreo_IoT_ESP32_PZEM (saved by Fritzing 1.0.5)
breadboards: 1

parts:
  esp1 = ESP32 DevKitc V4
  M1 = Pzem-004t

nets:
  N1: esp1.IO16, M1.TX
  N2: esp1.IO17, M1.RX
  GND: esp1.GND, M1.GND
  5V: esp1.5V, M1.5V

custom parts:
  ESP32 DevKitc V4: ESP32-DevKitC board with ESP32-WROOM-32 module. ESP32-DevKitC V4 is a small-sized ESP32-based development board produced by Espressif. Most of the pins on the ESP module are broken out to the pin headers on the board. The pins D0, D1, D2, D3, CMD and CLK are used internally for communication between ESP32 and SPI flash memory. They are grouped on both sides near the USB connector. Avoid using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
  Pzem-004t: Pzem-004t used for measuring AC voltage, current, active power, frequency, power factor and active energy, the module is without display function, the data is read through the TTL interface.
